# Fritzing sketch epiled_ambient (saved by Fritzing 0.9.3b)
breadboards: 1

parts:
  U1 = atmega168 [package=dip]
  Q1 = Basic FET N-Channel [package="TO220 [THT]"]
  Q2 = Basic FET N-Channel [package="TO220 [THT]"]
  Q3 = Basic FET N-Channel [package="TO220 [THT]"]
  XTAL1 = Crystal [frequency="16 Mhz" package=THT]
  C1 = Ceramic Capacitor [capacitance=22pF package="100 mil [THT, multilayer]"]
  C2 = Ceramic Capacitor [capacitance=22pF package="100 mil [THT, multilayer]"]
  U2 = Voltage Regulator - 5V [package="TO220 [THT]"]
  Power_plug1 = Power plug
  C3 = Ceramic Capacitor [capacitance=10nF package="100 mil [THT, multilayer]"]
  C4 = Electrolytic Capacitor [capacitance=22µF package="100 mil [THT, electrolytic]"]
  R1 = Resistor [tolerance=±5% resistance=1k package=THT]
  S1 = Pushbutton [package="[THT]"]
  LED1 = RGB LED (com. anode, rbg) [package="5 mm [THT]"]
  TRRS1 = Audio Jack (TRS) 3.5mm [package="4Ucon 08780 [THT]"]
  TRRS2 = Audio Jack (TRS) 3.5mm [package="PG203J [THT]"]

nets:
  N1: U1.RESET, R1.Pin_1, S1.Pin_1, S1.Pin_2
  N2: U1.VCC, U1.AVCC, U1.AREF, U2.output_voltage, C4.+, R1.Pin_0
  GND: U1.GND, U1.A5, Q1.drain, Q2.drain, Q3.drain, C1.1, C2.1, U2.GND, Power_plug1.GND, C3.0, C4.-, S1.Pin_3, S1.Pin_4, TRRS1.Tip, TRRS2.Sleeve, TRRS2.Ring, TRRS2.Tip
  N3: U1.XLAT1, XTAL1.pin_0, C2.0
  N4: U1.XLAT2, XTAL1.pin_1, C1.0
  N5: U1.D9_(PWM), Q1.gate
  N6: U1.D10_(PWM), Q2.gate
  N7: U1.D11_(PWM), Q3.gate
  N8: Q1.source, LED1.green_cathode
  N9: U2.input_voltage, Power_plug1.VCC, C3.1, LED1.common_anode
